// Logisim project cpu.circ as structural Verilog
// CPU
module main (
  input  clock,
  input  preset,
  input  unidade_de_controle_a_fazer,
  input  clear,
  output [15:0] \saída_da_memória ,
  output [7:0] debug_do_contador
);

  wire ULA_p2;

  contador_8bits Contador___8_bits (.clock(clock), .preset(preset), .clear(clear), .out_4(debug_do_contador));
  registrador_4bits Registrador_1 ();  // open: clock, preset, clear, q0, q1, q2, q3, d0, d1, d2, d3
  ROM #(.dataWidth(16), .Select("low")) ROM (.addr(debug_do_contador), .data(\saída_da_memória ));
  // ULA_main ULA: pin names not known; wires that end beside it: unidade_de_controle_a_fazer, ULA_p2, ULA_p2
  registrador_4bits Registrador_2 ();  // open: clock, preset, clear, q0, q1, q2, q3, d0, d1, d2, d3

  // Notes on the sheet:
  //   contents of ROM (hex, n*v repeats v):
  //   3000 239*0 23
endmodule

module contador_8bits (
  input  clock,
  input  preset,
  input  clear,
  output [7:0] out_4
);

  wire and_1_out, and_2_out, and_3_out, and_4_out, and_5_out, and_6_out;

  J_K_Flip_Flop j_k_ff_1 (.J(1'b1), .clk(clock), .K(1'b1), .Q(out_4[0]), .preset(clear), .reset(preset));  // open: Qn
  J_K_Flip_Flop j_k_ff_2 (
    .J(out_4[0]), .clk(clock), .K(out_4[0]), .Q(out_4[1]), .preset(clear), .reset(preset));  // open: Qn
  and and_1 (and_1_out, out_4[0], out_4[1]);
  J_K_Flip_Flop j_k_ff_3 (
    .J(and_1_out), .clk(clock), .K(and_1_out), .Q(out_4[2]), .preset(clear), .reset(preset));  // open: Qn
  and and_2 (and_2_out, and_1_out, out_4[2]);
  J_K_Flip_Flop j_k_ff_4 (
    .J(and_2_out), .clk(clock), .K(and_2_out), .Q(out_4[3]), .preset(clear), .reset(preset));  // open: Qn
  and and_3 (and_3_out, and_2_out, out_4[3]);
  J_K_Flip_Flop j_k_ff_5 (
    .J(and_3_out), .clk(clock), .K(and_3_out), .Q(out_4[4]), .preset(clear), .reset(preset));  // open: Qn
  and and_4 (and_4_out, and_3_out, out_4[4]);
  J_K_Flip_Flop j_k_ff_6 (
    .J(and_4_out), .clk(clock), .K(and_4_out), .Q(out_4[5]), .preset(clear), .reset(preset));  // open: Qn
  and and_5 (and_5_out, and_4_out, out_4[5]);
  J_K_Flip_Flop j_k_ff_7 (
    .J(and_5_out), .clk(clock), .K(and_5_out), .Q(out_4[6]), .preset(clear), .reset(preset));  // open: Qn
  and and_6 (and_6_out, and_5_out, out_4[6]);
  J_K_Flip_Flop j_k_ff_8 (
    .J(and_6_out), .clk(clock), .K(and_6_out), .Q(out_4[7]), .preset(clear), .reset(preset));  // open: Qn
endmodule

module registrador_4bits (
  input  clock,
  input  preset,
  input  clear,
  input  d0,
  input  d1,
  input  d2,
  input  d3,
  output q0,
  output q1,
  output q2,
  output q3
);

  wire d_ff_2_qn;

  D_Flip_Flop #(.Pre_Clr_Positions("LEGACY")) d_ff_1 (
    .clk(clock), .D(d0), .Q(q0), .preset(preset), .reset(clear));  // open: Qn
  D_Flip_Flop d_ff_2 (.clk(clock), .D(d1), .Q(q1), .Qn(d_ff_2_qn), .preset(preset), .reset(clear));
  D_Flip_Flop d_ff_3 (.clk(clock), .D(d2), .Q(q2), .preset(preset), .reset(clear));  // open: Qn
  D_Flip_Flop d_ff_4 (.clk(clock), .D(d3), .Q(q3), .reset(clear));  // open: Qn, preset
endmodule
